# Fritzing sketch tn_rpi2B_sketch (saved by Fritzing 0.9.3b)
circuit board: 8.46667cm x 5.64444cm
breadboards: 1

parts:
  LED2 = smd LED [color="Green (570nm)" package="0603 [SMD]"]
  LED3 = smd LED [color="Blue (430nm)" package="0603 [SMD]"]
  R2 = Resistor [tolerance=±5% resistance=220 package=THT]
  R4 = Resistor [tolerance=±5% resistance=220 package=THT]
  R6 = Resistor [tolerance=±5% resistance=220 package=THT]
  Raspberry_Pi1 = Raspberry Pi B+
  R7 = Resistor [tolerance=±5% resistance=220 package=THT]
  R8 = Resistor [tolerance=±5% resistance=220 package=THT]
  R1 = Resistor [tolerance=±5% resistance=220 package=THT]
  LED1 = smd LED [color="Red (633nm)" package="0603 [SMD]"]

nets:
  N1: LED2.cathode, R2.Pin_0
  N2: LED2.anode, Raspberry_Pi1.GPIO19
  N3: LED3.cathode, R6.Pin_0
  N4: LED3.anode, Raspberry_Pi1.GPIO13
  N5: R2.Pin_1, R1.Pin_0
  N6: R4.Pin_0, R6.Pin_1
  N7: R4.Pin_1, Raspberry_Pi1.GND, R7.Pin_1, R1.Pin_1
  N8: Raspberry_Pi1.GPIO26, LED1.anode
  N9: R7.Pin_0, R8.Pin_1
  N10: R8.Pin_0, LED1.cathode
